# Fritzing sketch Raspberry_Sharp_Sensor (saved by Fritzing 0.9.2b)
breadboards: 1

parts:
  Raspberry_Pi2 = Raspberry Pi B+
  IC1 = MCP3008 8-channel 10-bit ADC [part_number=MCP3008]
  J4 = Infrared Proximity Sensor

nets:
  N1: Raspberry_Pi2.GPIO25, IC1.no_name_yet#10
  N2: Raspberry_Pi2.GPIO24, IC1.no_name_yet#11
  N3: Raspberry_Pi2.GPIO23, IC1.no_name_yet#12
  N4: Raspberry_Pi2.GPIO18, IC1.no_name_yet#13
  GND: Raspberry_Pi2.GND, IC1.no_name_yet#9, IC1.no_name_yet#14, J4.GND
  5V: Raspberry_Pi2.5V, IC1.no_name_yet#15, IC1.no_name_yet#16, J4.Vcc
  N5: IC1.no_name_yet#1, J4.Vout
